# Fritzing sketch stellarduino_v1 (saved by Fritzing 0.9.1b)
breadboards: 1

parts:
  LCD1 = LCD screen
  S1 = Pushbutton [package="[THT]"]
  S2 = Pushbutton [package="[THT]"]
  S3 = Pushbutton [package="[THT]"]
  Part1 = Real Time Clock Module - DS1307 RTC Breakout Board
  U1 = RJ45 Jack [package=rj45-8]
  U2 = RJ45 Jack [package=rj45-8]
  Part2 = Arduino Uno (Rev3)
  R1 = Resistor [package="2512 [SMD]"]
  R2 = Resistor [package="2512 [SMD]"]
  R3 = Resistor [package="2512 [SMD]"]
  R4 = Resistor [package="2512 [SMD]"]

nets:
  GND: LCD1.VSS, LCD1.R/W, Part1.GND, U1.6, U2.6, Part2.GND
  5V: LCD1.VDD, S1.Pin_3, S1.Pin_4, S2.Pin_3, S2.Pin_4, S3.Pin_3, S3.Pin_4, Part1.5V, U1.8, U2.8, Part2.5V, R1.Pin_0, R2.Pin_0, R3.Pin_0, R4.Pin_0
  N1: LCD1.V0, R1.Pin_1
  N2: LCD1.RS, Part2.D6_PWM
  N3: LCD1.E, Part2.D7
  N4: LCD1.DB4, Part2.D8
  N5: LCD1.DB5, Part2.D9_PWM
  N6: LCD1.DB6, Part2.D10_PWM/SS
  N7: LCD1.DB7, Part2.D11_PWM/MOSI
  N8: S1.Pin_1, S1.Pin_2, Part2.A0, R2.Pin_1
  N9: S2.Pin_1, S2.Pin_2, Part2.A1, R3.Pin_1
  N10: S3.Pin_1, S3.Pin_2, Part2.A2, R4.Pin_1
  N11: Part1.SCL, Part2.A5/SCL
  N12: Part1.SDA, Part2.A4/SDA
  N13: U1.5, Part2.D4
  N14: U1.7, Part2.D2
  N15: U2.5, Part2.D5_PWM
  N16: U2.7, Part2.D3_PWM
